// Logisim project Nawal Ayesha_1911301042 Project.circ as structural Verilog
module _1_bit_ALU (
  input  [2:0] AluOp,
  input  A_invert,
  input  B_invert,
  input  C_in,
  input  A,
  input  B,
  output Result,
  output Carry_Out
);

  wire adder_1_out, and_1_out, multiplexer_1_out, multiplexer_2_out, not_1_out, not_2_out, or_1_out;

  not not_1 (not_1_out, A);
  not not_2 (not_2_out, B);
  Multiplexer #(.enable("false")) multiplexer_1 (.in0(A), .in1(not_1_out), .out(multiplexer_1_out), .sel(A_invert));
  Multiplexer #(.enable("false")) multiplexer_2 (.in0(B), .in1(not_2_out), .out(multiplexer_2_out), .sel(B_invert));
  and and_1 (and_1_out, multiplexer_1_out, multiplexer_2_out);
  or or_1 (or_1_out, multiplexer_1_out, multiplexer_2_out);
  Adder #(.width(1)) adder_1 (
    .a(multiplexer_1_out), .b(multiplexer_2_out), .out(adder_1_out), .cin(C_in), .cout(Carry_Out));
  Multiplexer #(.select(3), .enable("false")) multiplexer_3 (
    .in0(and_1_out), .in1(or_1_out), .in2(adder_1_out), .in3(or_1_out), .in4(and_1_out), .in6(adder_1_out),
    .in7(and_1_out), .out(Result), .sel(AluOp));  // open: in5
endmodule

module _13_bit_Multiplier (
  input  [12:0] A,
  input  [12:0] B,
  output [12:0] Product_S,
  output Mult_zero_flag
);

  wire or_1_out;
  wire [7:5] n4_bit_multiplier_2_s;

  _4_bit_Multiplier u_4_bit_multiplier_1 (.A(A[3:0]), .B(B[3:0]), .S(Product_S[7:0]));
  _4_bit_Multiplier u_4_bit_multiplier_2 (.A(A[7:4]), .B(B[7:4]), .S({n4_bit_multiplier_2_s, Product_S[12:8]}));
  or or_1 (or_1_out, Product_S[0], Product_S[1], Product_S[2], Product_S[3], Product_S[4], Product_S[5], Product_S[6], Product_S[7], Product_S[8], Product_S[9], Product_S[10], Product_S[11], Product_S[12]);
  not not_1 (Mult_zero_flag, or_1_out);
endmodule

module _4_bit_Multiplier (
  input  [3:0] A,
  input  [3:0] B,
  output [7:0] S
);

  wire [2:0] and_2_out;
  wire [3:0] and_5_out, and_9_out, and_13_out;
  wire [3:1] adder_1_out, adder_2_out;
  wire [3:3] adder_1_cout, adder_2_cout;

  and and_1 (S[0], A[0], B[0]);
  and and_2 (and_2_out[0], A[0], B[1]);
  and and_3 (and_2_out[1], A[0], B[2]);
  and and_4 (and_2_out[2], A[0], B[3]);
  and and_5 (and_5_out[0], A[1], B[0]);
  and and_6 (and_5_out[1], A[1], B[1]);
  and and_7 (and_5_out[2], A[1], B[2]);
  and and_8 (and_5_out[3], A[1], B[3]);
  Adder #(.width(4)) adder_1 (
    .a({1'b0, and_2_out}), .b(and_5_out), .out({adder_1_out, S[1]}), .cin(1'b0), .cout(adder_1_cout[3]));
  and and_9 (and_9_out[0], A[2], B[0]);
  and and_10 (and_9_out[1], A[2], B[1]);
  and and_11 (and_9_out[2], A[2], B[2]);
  and and_12 (and_9_out[3], A[2], B[3]);
  Adder #(.width(4)) adder_2 (
    .a({adder_1_cout[3], adder_1_out}), .b(and_9_out), .out({adder_2_out, S[2]}), .cin(1'b0),
    .cout(adder_2_cout[3]));
  and and_13 (and_13_out[0], A[3], B[0]);
  and and_14 (and_13_out[1], A[3], B[1]);
  and and_15 (and_13_out[2], A[3], B[2]);
  and and_16 (and_13_out[3], A[3], B[3]);
  Adder #(.width(4)) adder_3 (
    .a({adder_2_cout[3], adder_2_out}), .b(and_13_out), .out(S[6:3]), .cin(1'b0), .cout(S[7]));

  // Notes on the sheet:
  //   A1B1
  //   A1B2
  //   A1B3
  //   A1B4
  //   A2B1
  //   A2B2
  //   A2B3
  //   A2B4
  //   A3B1
  //   A3B2
  //   A3B3
  //   A3B4
  //   A4B1
  //   A4B2
  //   A4B3
  //   A4B4
endmodule

module _13_bit_ALU (
  input  [2:0] ALU_Op,
  input  C_in,
  input  B_inv,
  input  A_inv,
  input  [12:0] A,
  input  [12:0] B,
  output [12:0] Result,
  output Zero_Flag,
  output Overflow,
  output Carry_Out
);

  wire n1_bit_alu_1_carry_out, n1_bit_alu_2_carry_out, n1_bit_alu_3_carry_out, n1_bit_alu_4_carry_out,
       n1_bit_alu_5_carry_out, n1_bit_alu_6_carry_out, n1_bit_alu_7_carry_out, n1_bit_alu_8_carry_out,
       n1_bit_alu_9_carry_out, n1_bit_alu_10_carry_out, n1_bit_alu_11_carry_out, n1_bit_alu_12_carry_out,
       n13_bit_multiplier_1_mult_zero_flag, not_1_out, or_1_out;
  wire [12:0] n1_bit_alu_1_result, n13_bit_multiplier_1_product_s;

  _1_bit_ALU u_1_bit_alu_1 (
    .Result(n1_bit_alu_1_result[0]), .Carry_Out(n1_bit_alu_1_carry_out), .A(A[0]), .B(B[0]),
    .A_invert(A_inv), .B_invert(B_inv), .AluOp(ALU_Op), .C_in(C_in));
  _1_bit_ALU u_1_bit_alu_2 (
    .Result(n1_bit_alu_1_result[1]), .Carry_Out(n1_bit_alu_2_carry_out), .A(A[1]), .B(B[1]),
    .A_invert(A_inv), .B_invert(B_inv), .AluOp(ALU_Op), .C_in(n1_bit_alu_1_carry_out));
  _1_bit_ALU u_1_bit_alu_3 (
    .Result(n1_bit_alu_1_result[2]), .Carry_Out(n1_bit_alu_3_carry_out), .A(A[2]), .B(B[2]),
    .A_invert(A_inv), .B_invert(B_inv), .AluOp(ALU_Op), .C_in(n1_bit_alu_2_carry_out));
  _1_bit_ALU u_1_bit_alu_4 (
    .Result(n1_bit_alu_1_result[3]), .Carry_Out(n1_bit_alu_4_carry_out), .A(A[3]), .B(B[3]),
    .A_invert(A_inv), .B_invert(B_inv), .AluOp(ALU_Op), .C_in(n1_bit_alu_3_carry_out));
  _1_bit_ALU u_1_bit_alu_5 (
    .Result(n1_bit_alu_1_result[4]), .Carry_Out(n1_bit_alu_5_carry_out), .A(A[4]), .B(B[4]),
    .A_invert(A_inv), .B_invert(B_inv), .AluOp(ALU_Op), .C_in(n1_bit_alu_4_carry_out));
  _1_bit_ALU u_1_bit_alu_6 (
    .Result(n1_bit_alu_1_result[5]), .Carry_Out(n1_bit_alu_6_carry_out), .A(A[5]), .B(B[5]),
    .A_invert(A_inv), .B_invert(B_inv), .AluOp(ALU_Op), .C_in(n1_bit_alu_5_carry_out));
  _1_bit_ALU u_1_bit_alu_7 (
    .Result(n1_bit_alu_1_result[6]), .Carry_Out(n1_bit_alu_7_carry_out), .A(A[6]), .B(B[6]),
    .A_invert(A_inv), .B_invert(B_inv), .AluOp(ALU_Op), .C_in(n1_bit_alu_6_carry_out));
  _1_bit_ALU u_1_bit_alu_8 (
    .Result(n1_bit_alu_1_result[7]), .Carry_Out(n1_bit_alu_8_carry_out), .A(A[7]), .B(B[7]),
    .A_invert(A_inv), .B_invert(B_inv), .AluOp(ALU_Op), .C_in(n1_bit_alu_7_carry_out));
  _1_bit_ALU u_1_bit_alu_9 (
    .Result(n1_bit_alu_1_result[8]), .Carry_Out(n1_bit_alu_9_carry_out), .A(A[8]), .B(B[8]),
    .A_invert(A_inv), .B_invert(B_inv), .AluOp(ALU_Op), .C_in(n1_bit_alu_8_carry_out));
  _1_bit_ALU u_1_bit_alu_10 (
    .Result(n1_bit_alu_1_result[9]), .Carry_Out(n1_bit_alu_10_carry_out), .A(A[9]), .B(B[9]),
    .A_invert(A_inv), .B_invert(B_inv), .AluOp(ALU_Op), .C_in(n1_bit_alu_9_carry_out));
  _1_bit_ALU u_1_bit_alu_11 (
    .Result(n1_bit_alu_1_result[10]), .Carry_Out(n1_bit_alu_11_carry_out), .A(A[10]), .B(B[10]),
    .A_invert(A_inv), .B_invert(B_inv), .AluOp(ALU_Op), .C_in(n1_bit_alu_10_carry_out));
  _1_bit_ALU u_1_bit_alu_12 (
    .Result(n1_bit_alu_1_result[11]), .Carry_Out(n1_bit_alu_12_carry_out), .A(A[11]), .B(B[11]),
    .A_invert(A_inv), .B_invert(B_inv), .AluOp(ALU_Op), .C_in(n1_bit_alu_11_carry_out));
  _1_bit_ALU u_1_bit_alu_13 (
    .Result(n1_bit_alu_1_result[12]), .Carry_Out(Carry_Out), .A(A[12]), .B(B[12]), .A_invert(A_inv),
    .B_invert(B_inv), .AluOp(ALU_Op), .C_in(n1_bit_alu_12_carry_out));
  _13_bit_Multiplier u_13_bit_multiplier_1 (
    .A(A), .B(B), .Product_S(n13_bit_multiplier_1_product_s),
    .Mult_zero_flag(n13_bit_multiplier_1_mult_zero_flag));
  Multiplexer #(.select(3), .width(13), .enable("false")) multiplexer_1 (
    .in0(n1_bit_alu_1_result), .in1(n1_bit_alu_1_result), .in2(n1_bit_alu_1_result),
    .in3(n1_bit_alu_1_result), .in4(n1_bit_alu_1_result), .in6(n1_bit_alu_1_result),
    .in7(n13_bit_multiplier_1_product_s), .out(Result), .sel(ALU_Op));  // open: in5
  or or_1 (or_1_out, n1_bit_alu_1_result[0], n1_bit_alu_1_result[1], n1_bit_alu_1_result[2], n1_bit_alu_1_result[3], n1_bit_alu_1_result[4], n1_bit_alu_1_result[5], n1_bit_alu_1_result[6], n1_bit_alu_1_result[7], n1_bit_alu_1_result[8], n1_bit_alu_1_result[9], n1_bit_alu_1_result[10], n1_bit_alu_1_result[11], n1_bit_alu_1_result[12]);
  xor xor_1 (Overflow, n1_bit_alu_12_carry_out, Carry_Out);
  not not_1 (not_1_out, or_1_out);
  Multiplexer #(.select(3), .enable("false")) multiplexer_2 (
    .in0(not_1_out), .in1(not_1_out), .in2(not_1_out), .in3(not_1_out), .in4(not_1_out), .in6(not_1_out),
    .in7(n13_bit_multiplier_1_mult_zero_flag), .out(Zero_Flag), .sel(ALU_Op));  // open: in5
endmodule

module ALU_Control_NOR (
  input  C,
  input  B_invert,
  input  A_invert,
  input  F1,
  input  F0,
  output [2:0] ALU_Op
);

  wire CB_prime_A_prime_F1_prime_F0__prime_2_out, CB_prime_A_prime_F1_prime_F0__prime_out,
       CB_prime_A_prime_F1_prime_F0_prime__prime_out, CB_prime_F1_prime_F0__prime_out,
       CBAF1_prime__prime_out, CBAF1_prime_F0_prime__prime_2_out, CBAF1_prime_F0_prime__prime_out,
       CBAF1F0__prime_out, nor_1_out, nor_2_out, nor_3_out, nor_4_out, nor_5_out, nor_6_out, nor_7_out;

  nor nor_1 (nor_1_out, B_invert, B_invert);
  nor nor_2 (nor_2_out, A_invert, A_invert);
  nor nor_3 (nor_3_out, F1, F1);
  nor nor_4 (nor_4_out, F0, F0);
  nor CBAF1_prime_F0_prime__prime (CBAF1_prime_F0_prime__prime_out, C, B_invert, A_invert, nor_3_out, nor_4_out);
  nor CB_prime_A_prime_F1_prime_F0__prime (CB_prime_A_prime_F1_prime_F0__prime_out, C, nor_1_out, nor_2_out, nor_3_out, nor_4_out);
  nor CB_prime_A_prime_F1_prime_F0_prime__prime (CB_prime_A_prime_F1_prime_F0_prime__prime_out, C, nor_1_out, A_invert, nor_3_out, F0);
  nor CBAF1F0__prime (CBAF1F0__prime_out, C, B_invert, F1, A_invert, F0);
  nor CBAF1_prime_F0_prime__prime_2 (CBAF1_prime_F0_prime__prime_2_out, C, B_invert, A_invert, nor_3_out, nor_4_out);
  nor CB_prime_F1_prime_F0__prime (CB_prime_F1_prime_F0__prime_out, C, nor_1_out, nor_3_out, F0);
  nor CBAF1_prime__prime (CBAF1_prime__prime_out, C, B_invert, A_invert, nor_3_out);
  nor CB_prime_A_prime_F1_prime_F0__prime_2 (CB_prime_A_prime_F1_prime_F0__prime_2_out, C, nor_1_out, nor_2_out, nor_3_out, F0);
  nor nor_5 (nor_5_out, CBAF1F0__prime_out, CBAF1_prime_F0_prime__prime_2_out, CB_prime_F1_prime_F0__prime_out);
  nor nor_6 (nor_6_out, CBAF1_prime__prime_out, CB_prime_A_prime_F1_prime_F0__prime_2_out);
  nor nor_7 (nor_7_out, CBAF1_prime_F0_prime__prime_out, CB_prime_A_prime_F1_prime_F0__prime_out, CB_prime_A_prime_F1_prime_F0_prime__prime_out);
  nor y (ALU_Op[1], nor_5_out, nor_5_out);
  nor z (ALU_Op[0], nor_6_out, nor_6_out);
  nor x (ALU_Op[2], nor_7_out, nor_7_out);
endmodule

module Part_1 (
  input  C,
  input  B,
  input  A,
  input  F1,
  input  F0,
  input  C_In,
  input  [12:0] A_2,
  input  [12:0] B_2,
  output [2:0] out_9,
  output out_10,
  output [12:0] out_11,
  output out_12,
  output out_13
);

  ALU_Control_NOR alu_control_nor_1 (.ALU_Op(out_9), .C(C), .B_invert(B), .A_invert(A), .F1(F1), .F0(F0));
  _13_bit_ALU u_13_bit_alu_1 (
    .C_in(C_In), .B_inv(B), .A_inv(A), .A(A_2), .B(B_2), .Result(out_11), .Zero_Flag(out_10), .ALU_Op(out_9),
    .Carry_Out(out_13), .Overflow(out_12));
endmodule

module Part_2 (
  input  in_1,
  input  CLR,
  output [3:0] Address_of_next_instruction,
  output [1:0] Op,
  output [2:0] rd,
  output [3:0] out_6,
  output [2:0] rs,
  output [2:0] rt,
  output [1:0] funct
);

  wire CLK_out;

  Clock CLK (.out(CLK_out));
  Register #(.width(4)) register_1 (.D(Address_of_next_instruction), .en(1'b1), .Q(out_6), .clk(CLK_out), .clr(CLR));
  ROM #(.addrWidth(4), .dataWidth(13)) rom_1 (.addr(out_6), .data({Op, rd, rs, rt, funct}));  // open: sel
  Adder #(.width(4)) adder_1 (.a(4'b0001), .b(out_6), .out(Address_of_next_instruction), .cin(in_1));  // open: cout

  // Notes on the sheet:
  //   PC
  //   Address
  //   contents of rom_1 (hex, n*v repeats v):
  //   322 213 43 a10 1f1 110 1101 1111 11 10 43 1001 1010 1011 1110 101
  //   Instruction
endmodule
